# Fritzing sketch ArduinoServoMPU6050 (saved by Fritzing 0.7.12b)
breadboards: 1

parts:
  Arduino2 = Arduino
  J1 = Basic Servo
  J2 = Basic Servo
  J3 = Basic Servo
  Componente1 = Tri-Axis Gyro Breakout - L3G4200D

nets:
  GND: Arduino2.GND, J1.gnd, J2.gnd, J3.gnd, Componente1.GND
  N1: Arduino2.D11, J1.pulse
  N2: Arduino2.D10, J3.pulse
  N3: Arduino2.D9, J2.pulse
  VCC: Arduino2.+5V, J1.vcc, J2.vcc, J3.vcc, Componente1.VCC
  N4: Arduino2.A4, Componente1.SDA
  N5: Arduino2.A5, Componente1.SCL
